# Fritzing sketch Cloud Point (saved by Fritzing 0.9.3b)
circuit board: 8.46667cm x 5.64444cm
breadboards: 2

parts:
  Part1 = Arduino Uno (Rev3)
  R1 = Resistor [tolerance=±5% resistance=10k package=THT]
  Adafruit_Breakout = Adafruit MAX31865 RTD Sensor Breakout [part_number="Adafruit #3328"]
  R2 = Photocell (LDR) [package=THT]
  LTC_1050 = IC, DIP package, 8 pins [chip_label="LTC 1050"]
  C1 = Ceramic Capacitor [capacitance=100nF package="100 mil [THT, multilayer]"]
  J1 = JST-B3P-VH [part_number=JST-B3P-VH package=THT]

nets:
  N1: Part1.A0, R1.Pin_1, LTC_1050.pin6, C1.1
  N2: Part1.D10_PWM/SS, Adafruit_Breakout.CS
  N3: Part1.D11_PWM/MOSI, Adafruit_Breakout.SDI
  N4: Part1.D12/MISO, Adafruit_Breakout.SDO
  N5: Part1.D13/SCK, Adafruit_Breakout.SCLK
  5V: Part1.5V, Adafruit_Breakout.VIN, LTC_1050.pin7
  GND: Part1.GND, Adafruit_Breakout.GND, R2.pin_0, LTC_1050.pin3, LTC_1050.pin4, J1.pin2, J1.pin1
  N6: R1.Pin_0, R2.pin_1, LTC_1050.pin2, C1.0, J1.pin3

notes:
  Photodiode Detector Board
  Amplifier Board
  5 mW 650 nm Laser Diode
  Adafruit MAX31865 RTD Amplifier
  3-Wire PT100 RTD Probe
  GRR-1000 CLOUDPOINT
  MICHAEL J. A. HORE

custom parts:
  Adafruit MAX31865 RTD Sensor Breakout: For precision temperature sensing, nothing beats a Platinum RTD. Resistance temperature detectors (RTDs) are temperature sensors that contain a resistor that changes resistance value as its temperature changes, basically a kind of thermistor. In this sensor, the resistor is actually a small strip of Platinum with a resistance of 100 ohms at 0°C, thus the name PT100. Compared to most NTC/PTC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
